// Logisim project finprojZ.circ as structural Verilog: 1 circuit, main circuit main
module main (
  input  in_1,
  input  in_2,
  input  in_3,
  input  in_4,
  input  in_5
);

  wire and_1_out, and_2_out, and_3_out, and_4_out, and_5_out, and_6_out, and_7_out, and_8_out, and_9_out,
       and_10_out, and_11_out, and_12_out, and_13_out, and_14_out, and_15_out, and_16_out, and_17_out,
       and_18_out, and_19_out, and_20_out, and_21_out, and_22_out, and_23_out, and_24_out, and_25_out,
       and_26_out, and_27_out, and_28_out, and_29_out, and_30_out, and_31_out, and_32_out, and_33_out,
       and_34_out, and_35_out, and_36_out, and_37_out, and_38_out, and_39_out, and_40_out, and_41_out,
       and_42_out, and_43_out, and_44_out, and_45_out, and_46_out, and_47_out, and_48_out, and_49_out,
       and_50_out, and_51_out, and_52_out, and_53_out, and_54_out, and_55_out, and_56_out, and_57_out,
       and_58_out, and_59_out, and_60_out, and_61_out, and_62_out, and_63_out, and_64_out, and_65_out,
       and_66_out, and_67_out, and_68_out, and_69_out, and_70_out, and_71_out, and_72_out, and_73_out,
       and_74_out, and_75_out, and_76_out, and_77_out, and_78_out, and_79_out, and_80_out, and_81_out,
       and_82_out, and_83_out, and_84_out, and_85_out, and_86_out, and_87_out, and_88_out, and_90_out,
       clock_1_out, d_ff_1_q, d_ff_2_q, d_ff_3_q, d_ff_4_q, d_ff_5_q, d_ff_6_q, d_ff_7_q, d_ff_8_q, d_ff_9_q,
       d_ff_10_q, d_ff_11_q, d_ff_12_q, d_ff_13_q, d_ff_14_q, d_ff_15_q, d_ff_16_q, d_ff_17_q, d_ff_18_q,
       d_ff_19_q, d_ff_20_q, d_ff_21_q, d_ff_22_q, d_ff_23_q, d_ff_24_q, d_ff_25_q, d_ff_26_q, d_ff_27_q,
       d_ff_28_q, d_ff_29_q, d_ff_30_q, d_ff_31_q, d_ff_32_q, d_ff_33_q, d_ff_34_q, d_ff_35_q, d_ff_36_q,
       d_ff_37_q, d_ff_38_q, d_ff_39_q, d_ff_40_q, d_ff_41_q, d_ff_42_q, d_ff_43_q, d_ff_44_q, not_1_out,
       not_2_out, not_3_out, not_4_out, not_5_out, not_6_out, not_7_out, not_8_out, not_9_out, not_10_out,
       not_11_out, not_12_out, not_13_out, not_14_out, not_15_out, not_16_out, not_17_out, not_18_out,
       not_19_out, not_20_out, not_21_out, not_22_out, not_23_out, not_24_out, or_1_out, or_2_out, or_3_out,
       or_4_out, or_5_out, or_6_out, or_7_out, undriven, undriven_2, undriven_3, undriven_4, undriven_5,
       undriven_6, undriven_7, undriven_8, undriven_9, undriven_10, undriven_11, undriven_12, undriven_13,
       undriven_14, undriven_15, undriven_16, undriven_17, undriven_18, undriven_19, undriven_20, xor_1_out,
       xor_2_out, xor_3_out;

  D_Flip_Flop #(.trigger("falling")) d_ff_1 (
    .D(xor_1_out), .clk(clock_1_out), .Q(d_ff_1_q));  // open: Qn, preset, reset
  xor xor_1 (xor_1_out, and_1_out, d_ff_1_q);
  and and_1 (and_1_out, d_ff_2_q, and_2_out);
  D_Flip_Flop #(.trigger("falling")) d_ff_2 (
    .D(xor_2_out), .clk(clock_1_out), .Q(d_ff_2_q));  // open: Qn, preset, reset
  Clock clock_1 (.out(clock_1_out));
  not not_1 (not_1_out, d_ff_3_q);
  not not_2 (not_2_out, d_ff_2_q);
  not not_3 (not_3_out, d_ff_2_q);
  not not_4 (not_4_out, d_ff_3_q);
  not not_5 (not_5_out, d_ff_1_q);
  not not_6 (not_6_out, d_ff_1_q);
  not not_7 (not_7_out, d_ff_3_q);
  not not_8 (not_8_out, d_ff_1_q);
  not not_9 (not_9_out, d_ff_2_q);
  not not_10 (not_10_out, d_ff_1_q);
  not not_11 (not_11_out, d_ff_2_q);
  not not_12 (not_12_out, d_ff_3_q);
  D_Flip_Flop #(.trigger("falling")) d_ff_3 (
    .D(xor_3_out), .clk(clock_1_out), .Q(d_ff_3_q));  // open: Qn, preset, reset
  xor xor_2 (xor_2_out, and_2_out, d_ff_2_q);
  and and_2 (and_2_out, or_1_out, d_ff_3_q);
  and and_3 (and_3_out, d_ff_1_q, d_ff_2_q, clock_1_out, d_ff_3_q);
  and and_4 (and_4_out, d_ff_1_q, d_ff_2_q, clock_1_out, not_1_out);
  and and_5 (and_5_out, d_ff_1_q, not_2_out, clock_1_out, d_ff_3_q);
  and and_6 (and_6_out, d_ff_1_q, not_3_out, clock_1_out, not_4_out);
  and and_7 (and_7_out, not_5_out, d_ff_2_q, clock_1_out, d_ff_3_q);
  and and_8 (and_8_out, not_6_out, d_ff_2_q, clock_1_out, not_7_out);
  and and_9 (and_9_out, not_8_out, not_9_out, clock_1_out, d_ff_3_q);
  and and_10 (and_10_out, not_10_out, not_11_out, clock_1_out, not_12_out);
  and and_11 (and_11_out, and_3_out, not_13_out);
  and and_12 (and_12_out, and_4_out, not_13_out);
  and and_13 (and_13_out, and_5_out, not_13_out);
  and and_14 (and_14_out, and_6_out, not_13_out);
  and and_15 (and_15_out, and_7_out, not_13_out);
  and and_16 (and_16_out, and_8_out, not_13_out);
  and and_17 (and_17_out, and_9_out, not_13_out);
  and and_18 (and_18_out, and_10_out, not_13_out);
  not not_13 (not_13_out, d_ff_4_q);
  D_Flip_Flop #(.trigger("falling")) d_ff_4 (.D(in_1), .clk(clock_1_out), .Q(d_ff_4_q));  // open: Qn, preset, reset
  xor xor_3 (xor_3_out, d_ff_3_q, or_1_out);
  or or_1 (or_1_out, d_ff_3_q, not_14_out);
  not not_14 (not_14_out, d_ff_3_q);
  D_Flip_Flop #(.trigger("high")) d_ff_5 (.D(and_19_out), .clk(and_11_out), .Q(d_ff_5_q));  // open: Qn, preset, reset
  and and_19 (and_19_out, and_3_out, not_13_out, d_ff_13_q);
  D_Flip_Flop #(.trigger("high")) d_ff_6 (.D(and_20_out), .clk(and_12_out), .Q(d_ff_6_q));  // open: Qn, preset, reset
  and and_20 (and_20_out, and_4_out, not_13_out, d_ff_13_q);
  and and_21 (and_21_out, and_5_out, not_13_out, d_ff_13_q);
  D_Flip_Flop #(.trigger("high")) d_ff_7 (.D(and_21_out), .clk(and_13_out), .Q(d_ff_7_q));  // open: Qn, preset, reset
  and and_22 (and_22_out, and_6_out, not_13_out, d_ff_13_q);
  D_Flip_Flop #(.trigger("high")) d_ff_8 (.D(and_22_out), .clk(and_14_out), .Q(d_ff_8_q));  // open: Qn, preset, reset
  D_Flip_Flop #(.trigger("high")) d_ff_9 (.D(and_23_out), .clk(and_15_out), .Q(d_ff_9_q));  // open: Qn, preset, reset
  and and_23 (and_23_out, and_7_out, not_13_out, d_ff_13_q);
  D_Flip_Flop #(.trigger("high")) d_ff_10 (.D(and_24_out), .clk(and_16_out), .Q(d_ff_10_q));  // open: Qn, preset, reset
  and and_24 (and_24_out, and_8_out, not_13_out, d_ff_13_q);
  and and_25 (and_25_out, and_9_out, not_13_out, d_ff_13_q);
  D_Flip_Flop #(.trigger("high")) d_ff_11 (.D(and_25_out), .clk(and_17_out), .Q(d_ff_11_q));  // open: Qn, preset, reset
  D_Flip_Flop #(.trigger("high")) d_ff_12 (.D(and_26_out), .clk(and_18_out), .Q(d_ff_12_q));  // open: Qn, preset, reset
  and and_26 (and_26_out, and_10_out, not_13_out, d_ff_13_q);
  or or_2 (or_2_out, and_27_out, and_28_out, and_29_out, and_30_out, and_31_out, and_32_out, and_33_out, and_34_out);
  and and_27 (and_27_out, d_ff_5_q, and_3_out, d_ff_4_q);
  and and_28 (and_28_out, d_ff_6_q, and_4_out, d_ff_4_q);
  and and_29 (and_29_out, d_ff_7_q, and_5_out, d_ff_4_q);
  and and_30 (and_30_out, d_ff_8_q, and_6_out, d_ff_4_q);
  and and_31 (and_31_out, d_ff_9_q, and_7_out, d_ff_4_q);
  and and_32 (and_32_out, d_ff_10_q, and_8_out, d_ff_4_q);
  and and_33 (and_33_out, d_ff_11_q, and_9_out, d_ff_4_q);
  and and_34 (and_34_out, d_ff_12_q, and_10_out, d_ff_4_q);
  D_Flip_Flop #(.trigger("falling")) d_ff_13 (.D(in_2), .clk(clock_1_out), .Q(d_ff_13_q));  // open: Qn, preset, reset
  D_Flip_Flop #(.trigger("falling")) d_ff_14 (.D(in_3), .clk(clock_1_out), .Q(d_ff_14_q));  // open: Qn, preset, reset
  D_Flip_Flop #(.trigger("high")) d_ff_15 (.D(and_35_out), .clk(and_11_out), .Q(d_ff_15_q));  // open: Qn, preset, reset
  and and_35 (and_35_out, and_3_out, not_13_out, d_ff_14_q);
  and and_36 (and_36_out, and_4_out, not_13_out, d_ff_14_q);
  D_Flip_Flop #(.trigger("high")) d_ff_16 (.D(and_36_out), .clk(and_12_out), .Q(d_ff_16_q));  // open: Qn, preset, reset
  and and_37 (and_37_out, and_5_out, not_13_out, d_ff_14_q);
  D_Flip_Flop #(.trigger("high")) d_ff_17 (.D(and_37_out), .clk(and_13_out), .Q(d_ff_17_q));  // open: Qn, preset, reset
  D_Flip_Flop #(.trigger("high")) d_ff_18 (.D(and_38_out), .clk(and_14_out), .Q(d_ff_18_q));  // open: Qn, preset, reset
  and and_38 (and_38_out, and_6_out, not_13_out, d_ff_14_q);
  and and_39 (and_39_out, and_7_out, not_13_out, d_ff_14_q);
  D_Flip_Flop #(.trigger("high")) d_ff_19 (.D(and_39_out), .clk(and_15_out), .Q(d_ff_19_q));  // open: Qn, preset, reset
  D_Flip_Flop #(.trigger("high")) d_ff_20 (.D(and_40_out), .clk(and_16_out), .Q(d_ff_20_q));  // open: Qn, preset, reset
  and and_40 (and_40_out, and_8_out, not_13_out, d_ff_14_q);
  and and_41 (and_41_out, and_9_out, not_13_out, d_ff_14_q);
  D_Flip_Flop #(.trigger("high")) d_ff_21 (.D(and_41_out), .clk(and_17_out), .Q(d_ff_21_q));  // open: Qn, preset, reset
  and and_42 (and_42_out, and_10_out, not_13_out, d_ff_14_q);
  D_Flip_Flop #(.trigger("high")) d_ff_22 (.D(and_42_out), .clk(and_18_out), .Q(d_ff_22_q));  // open: Qn, preset, reset
  D_Flip_Flop #(.trigger("falling")) d_ff_23 (.D(in_4), .clk(clock_1_out), .Q(d_ff_23_q));  // open: Qn, preset, reset
  D_Flip_Flop #(.trigger("high")) d_ff_24 (.D(or_2_out), .clk(clock_1_out), .Q(d_ff_24_q));  // open: Qn, preset, reset
  and and_43 (and_43_out, d_ff_15_q, and_3_out, d_ff_4_q);
  and and_44 (and_44_out, d_ff_16_q, and_4_out, d_ff_4_q);
  and and_45 (and_45_out, d_ff_17_q, and_5_out, d_ff_4_q);
  and and_46 (and_46_out, d_ff_18_q, and_6_out, d_ff_4_q);
  and and_47 (and_47_out, d_ff_19_q, and_7_out, d_ff_4_q);
  and and_48 (and_48_out, d_ff_20_q, and_8_out, d_ff_4_q);
  and and_49 (and_49_out, d_ff_21_q, and_9_out, d_ff_4_q);
  and and_50 (and_50_out, d_ff_22_q, and_10_out, d_ff_4_q);
  D_Flip_Flop #(.trigger("falling")) d_ff_25 (.D(in_5), .clk(clock_1_out), .Q(d_ff_25_q));  // open: Qn, preset, reset
  D_Flip_Flop #(.trigger("high")) d_ff_26 (.D(or_3_out), .clk(clock_1_out), .Q(d_ff_26_q));  // open: Qn, preset, reset
  or or_3 (or_3_out, and_43_out, and_44_out, and_45_out, and_46_out, and_47_out, and_48_out, and_49_out, and_50_out);
  D_Flip_Flop #(.trigger("high")) d_ff_27 (.D(or_4_out), .clk(clock_1_out), .Q(d_ff_27_q));  // open: Qn, preset, reset
  D_Flip_Flop #(.trigger("high")) d_ff_28 (.D(or_5_out), .clk(clock_1_out), .Q(d_ff_28_q));  // open: Qn, preset, reset
  and and_51 (and_51_out, and_3_out, not_13_out, d_ff_23_q);
  D_Flip_Flop #(.trigger("high")) d_ff_29 (.D(and_51_out), .clk(and_11_out), .Q(d_ff_29_q));  // open: Qn, preset, reset
  and and_52 (and_52_out, and_4_out, not_13_out, d_ff_23_q);
  D_Flip_Flop #(.trigger("high")) d_ff_30 (.D(and_52_out), .clk(and_12_out), .Q(d_ff_30_q));  // open: Qn, preset, reset
  and and_53 (and_53_out, and_5_out, not_13_out, d_ff_23_q);
  D_Flip_Flop #(.trigger("high")) d_ff_31 (.D(and_53_out), .clk(and_13_out), .Q(d_ff_31_q));  // open: Qn, preset, reset
  D_Flip_Flop #(.trigger("high")) d_ff_32 (.D(and_54_out), .clk(and_14_out), .Q(d_ff_32_q));  // open: Qn, preset, reset
  and and_54 (and_54_out, and_6_out, not_13_out, d_ff_23_q);
  D_Flip_Flop #(.trigger("high")) d_ff_33 (.D(and_55_out), .clk(and_15_out), .Q(d_ff_33_q));  // open: Qn, preset, reset
  and and_55 (and_55_out, and_7_out, not_13_out, d_ff_23_q);
  D_Flip_Flop #(.trigger("high")) d_ff_34 (.D(and_56_out), .clk(and_16_out), .Q(d_ff_34_q));  // open: Qn, preset, reset
  and and_56 (and_56_out, and_8_out, not_13_out, d_ff_23_q);
  D_Flip_Flop #(.trigger("high")) d_ff_35 (.D(and_57_out), .clk(and_17_out), .Q(d_ff_35_q));  // open: Qn, preset, reset
  and and_57 (and_57_out, and_9_out, not_13_out, d_ff_23_q);
  and and_58 (and_58_out, and_10_out, not_13_out, d_ff_23_q);
  D_Flip_Flop #(.trigger("high")) d_ff_36 (.D(and_58_out), .clk(and_18_out), .Q(d_ff_36_q));  // open: Qn, preset, reset
  or or_4 (or_4_out, and_59_out, and_60_out, and_61_out, and_62_out, and_63_out, and_64_out, and_65_out, and_66_out);
  and and_59 (and_59_out, d_ff_29_q, and_3_out, d_ff_4_q);
  and and_60 (and_60_out, d_ff_30_q, and_4_out, d_ff_4_q);
  and and_61 (and_61_out, d_ff_31_q, and_5_out, d_ff_4_q);
  and and_62 (and_62_out, d_ff_32_q, and_6_out, d_ff_4_q);
  and and_63 (and_63_out, d_ff_33_q, and_7_out, d_ff_4_q);
  and and_64 (and_64_out, d_ff_34_q, and_8_out, d_ff_4_q);
  and and_65 (and_65_out, d_ff_35_q, and_9_out, d_ff_4_q);
  and and_66 (and_66_out, d_ff_36_q, and_10_out, d_ff_4_q);
  and and_67 (and_67_out, and_3_out, not_13_out, d_ff_25_q);
  D_Flip_Flop #(.trigger("high")) d_ff_37 (.D(and_67_out), .clk(and_11_out), .Q(d_ff_37_q));  // open: Qn, preset, reset
  and and_68 (and_68_out, and_4_out, not_13_out, d_ff_25_q);
  D_Flip_Flop #(.trigger("high")) d_ff_38 (.D(and_68_out), .clk(and_12_out), .Q(d_ff_38_q));  // open: Qn, preset, reset
  D_Flip_Flop #(.trigger("high")) d_ff_39 (.D(and_69_out), .clk(and_13_out), .Q(d_ff_39_q));  // open: Qn, preset, reset
  and and_69 (and_69_out, and_5_out, not_13_out, d_ff_25_q);
  D_Flip_Flop #(.trigger("high")) d_ff_40 (.D(and_70_out), .clk(and_14_out), .Q(d_ff_40_q));  // open: Qn, preset, reset
  and and_70 (and_70_out, and_6_out, not_13_out, d_ff_25_q);
  D_Flip_Flop #(.trigger("high")) d_ff_41 (.D(and_71_out), .clk(and_15_out), .Q(d_ff_41_q));  // open: Qn, preset, reset
  and and_71 (and_71_out, and_7_out, not_13_out, d_ff_25_q);
  and and_72 (and_72_out, and_8_out, not_13_out, d_ff_25_q);
  D_Flip_Flop #(.trigger("high")) d_ff_42 (.D(and_72_out), .clk(and_16_out), .Q(d_ff_42_q));  // open: Qn, preset, reset
  and and_73 (and_73_out, and_9_out, not_13_out, d_ff_25_q);
  D_Flip_Flop #(.trigger("high")) d_ff_43 (.D(and_73_out), .clk(and_17_out), .Q(d_ff_43_q));  // open: Qn, preset, reset
  D_Flip_Flop #(.trigger("high")) d_ff_44 (.D(and_74_out), .clk(and_18_out), .Q(d_ff_44_q));  // open: Qn, preset, reset
  and and_74 (and_74_out, and_10_out, not_13_out, d_ff_25_q);
  or or_5 (or_5_out, and_75_out, and_76_out, and_77_out, and_78_out, and_79_out, and_80_out, and_81_out, and_82_out);
  and and_75 (and_75_out, d_ff_37_q, and_3_out, d_ff_4_q);
  and and_76 (and_76_out, d_ff_38_q, and_4_out, d_ff_4_q);
  and and_77 (and_77_out, d_ff_39_q, and_5_out, d_ff_4_q);
  and and_78 (and_78_out, d_ff_40_q, and_6_out, d_ff_4_q);
  and and_79 (and_79_out, d_ff_41_q, and_7_out, d_ff_4_q);
  and and_80 (and_80_out, d_ff_42_q, and_8_out, d_ff_4_q);
  and and_81 (and_81_out, d_ff_43_q, and_9_out, d_ff_4_q);
  and and_82 (and_82_out, d_ff_44_q, and_10_out, d_ff_4_q);
  not not_15 (not_15_out, undriven_5);
  not not_16 (not_16_out, undriven_6);
  not not_17 (not_17_out, undriven_9);
  not not_18 (not_18_out, undriven_12);
  not not_19 (not_19_out, undriven_3);
  not not_20 (not_20_out, undriven_4);
  and and_83 (and_83_out, not_15_out, not_16_out);
  or or_6 (or_6_out, undriven_7, undriven_8);
  and and_84 (and_84_out, not_17_out, undriven_10);
  and and_85 (and_85_out, undriven_11, not_18_out);
  and and_86 (and_86_out, undriven, undriven_2);
  or or_7 (or_7_out, not_19_out, not_20_out);
  and and_87 (and_87_out, undriven_13, undriven_14, undriven_15, undriven_16);
  not not_21 (not_21_out, undriven_17);
  not not_22 (not_22_out, undriven_18);
  and and_88 (and_88_out, not_21_out, not_22_out, not_23_out, not_24_out);
  not not_23 (not_23_out, undriven_19);
  not not_24 (not_24_out, undriven_20);
  // AND_Gate and_89 has open pins: in0=and_83_out, in1=or_6_out, out=open
  and and_90 (and_90_out, and_86_out, or_7_out);

  // Notes on the sheet:
  //   ADD 1
  //   3-bit address input pins
  //   PROGRAM COUNTER
  //   Mode input pin
  //   4-bit data input pins
  //   INSTRUCTION REGISTER
  //   INSTRUCTION RAM
  //   LSB
  //   MSB
  //   IDENTIFY OPCODE
  //   COULD BE REPLACED WITH DECODER
  //   00--load
  //    01--save
  //   10--add
  //   11--sub
  //   SPECIAL CASES
  //   HALT
  //   JUMP
  //   CONTROL UNIT
  //   ALU (amruth)
endmodule
